# Fritzing sketch flora_breadboard_rev05 (saved by Fritzing 0.9.4)
perfboards: 1

parts:
  J1 = Terminal Block - 3 pins [part_number=Power package=THT]
  R1 = Resistor [tolerance=±5% resistance=1k package=THT]
  U1 = BTS621 [package="TO220 7-Lead [THT]"]
  J2 = Terminal Block - 3 pins [part_number="Tank Sensors" package=THT]
  R2 = Resistor [tolerance=±5% resistance=470 package=THT]
  R3 = Resistor [tolerance=±5% resistance=470 package=THT]
  R4 = Resistor [tolerance=±5% resistance=330 package=THT]
  R5 = Resistor [tolerance=±5% resistance=330 package=THT]
  R6 = Resistor [tolerance=±5% resistance=560 package=THT]
  R7 = Resistor [tolerance=±5% resistance=560 package=THT]
  J3 = Terminal Block - 3 pins [part_number=Pump package=THT]
  R8 = Resistor [tolerance=±5% resistance=3.3k package=THT]
  R9 = Resistor [tolerance=±5% resistance=3.3k package=THT]
  JP1 = Header 6 [part_number="Socket Header" package=1x06_smd_straight_alt]
  J4 = Generic shrouded header - 26 pins [part_number="Raspberry Pi" form="♂ (shrouded male)" package=THT]

nets:
  N1: J1.Line_1, U1.Vbb
  GND: J1.Line_2, U1.GND, J2.Line_3, R6.Pin_1, R7.Pin_1, J3.Line_3, R8.Pin_0, R9.Pin_0, JP1.5, J4.pin6, J4.pin9, J4.pin14, J4.pin20, J4.pin25
  5V-2: J1.Line_3, R2.Pin_0, R3.Pin_0, J4.pin4
  3V3: R1.Pin_0, J4.pin1
  GPIO22: R1.Pin_1, U1.ST, J4.pin15
  GPIO17_RTS: U1.IN2, R9.Pin_1, J4.pin11
  N2: U1.OUT2, J3.Line_2
  N3: U1.OUT1, J3.Line_1
  GPIO27: U1.IN1, R8.Pin_1, J4.pin13
  N4: J2.Line_1, R2.Pin_1, R4.Pin_0
  N5: J2.Line_2, R3.Pin_1, R5.Pin_0
  GPIO23: R4.Pin_1, R6.Pin_0, J4.pin16
  GPIO24: R5.Pin_1, R7.Pin_0, J4.pin18
  3V3-2: JP1.1, JP1.2, JP1.6, J4.pin17
  GPIO2_SDA: JP1.3, J4.pin3
  GPIO3_SCL: JP1.4, J4.pin5
  5V: J4.pin2
  GPIO4: J4.pin7
  GPIO14_TXD: J4.pin8
  GPIO15_RXD: J4.pin10
  GPIO18_PWM: J4.pin12
  GPIO10_MOSI: J4.pin19
  GPIO9_MISO: J4.pin21
  GPIO25: J4.pin22
  GPIO11_CLK: J4.pin23
  GPIO8_CE0: J4.pin24
  GPIO7_CE1: J4.pin26

notes:
  GND
  VCC
  SCK/SCL
  SDI/SDA
  CSB
  SDO/ADDR
  12V
  5V
  Tank_low
  Tank_empty
  Out1
  Out2
  Flora, Raspberry Pi Irrigation Controller, 0.5

custom parts:
  Terminal Block - 3 pins: Generic Screw Terminal 9.5mm
  BTS621: Smart Two Channel Highside Power Switch
  Generic shrouded header - 26 pins: Generic shrouded header
